# Fritzing sketch Sketch (saved by Fritzing 0.9.6b)

parts:
  A1 = Raspberry Pi Pico W
  M1 = BME680 Module [part_number=CJMCU-680]
  TP1 = TP4056 [chip_label=TP4056 package="DIP (Dual Inline) [THT]"]
  BAT1 = 18650 battery holder [package=battery-18650-kit]
  Part1 = Solar Cell

nets:
  N1: A1.pin_3, A1.pin_38, A1.pin_42, M1.GND, TP1.pin6
  N2: A1.pin_10, M1.SCL
  N3: A1.pin_11, M1.SDA
  N4: A1.pin_36, M1.VCC
  N5: A1.pin_39, TP1.pin3
  N6: TP1.pin1, Part1.+
  N7: TP1.pin2, Part1.-
  N8: TP1.pin4, BAT1.-
  N9: TP1.pin5, BAT1.+

custom parts:
  Raspberry Pi Pico W: Raspberry Pi Pico W. Based around the RP2040 microcontroller the Pico W is a low cost microcontroller device bringing Raspberry Pi quality, cost, and easy of use to the microcontroller space. The areas marked KEEPOUT in pcb silkscreen should not have traces running through them to avoid shorts on a soldered in module!
  BME680 Module: Bosch BME680 Development Module The BME680 is a digital 4-in-1 sensor that measures air quality [gas], humidity, pressure and temperature. Links: BME680 product datasheet
  TP4056: A DIP stand-in part for whatever IC you want. With 6 pins on a 300mil dual inline package (DIP) footprint.
  18650 battery holder: 18650 Battery
